# Fritzing sketch BionicArm (saved by Fritzing 0.9.3b)
breadboards: 2

parts:
  J1 = Basic Servo  # not connected
  J2 = Basic Servo  # not connected
  J3 = Basic Servo  # not connected
  J4 = Basic Servo  # not connected
  J5 = Basic Servo  # not connected
  BAT1 = BC9VPC [package=bc9vpc]  # not connected
  Part1 = Arduino Uno (Rev3)
  R1 = Basic Flex Resistor
  R2 = Basic Flex Resistor
  R3 = Basic Flex Resistor
  R4 = Basic Flex Resistor
  R5 = Basic Flex Resistor
  R6 = Resistor [tolerance=±5% resistance=220 package="1206 [SMD]"]
  R7 = Resistor [tolerance=±5% resistance=220 package="1206 [SMD]"]
  R8 = Resistor [tolerance=±5% resistance=220 package="1206 [SMD]"]
  R9 = Resistor [tolerance=±5% resistance=220 package="1206 [SMD]"]
  R10 = Resistor [tolerance=±5% resistance=220 package="1206 [SMD]"]
  J6 = female pin header, 2 pins [form="♀ (female)"]  # not connected
  J7 = female pin header, 2 pins [form="♀ (female)"]  # not connected
  J9 = female pin header, 2 pins [form="♀ (female)"]  # not connected
  J10 = female pin header, 2 pins [form="♀ (female)"]  # not connected
  J8 = female pin header, 2 pins [form="♀ (female)"]  # not connected

nets:
  N1: Part1.5V, R6.Pin_1, R7.Pin_1, R8.Pin_1, R9.Pin_1, R10.Pin_1
  N2: Part1.GND, R1.pin_1, R2.pin_1, R3.pin_1, R4.pin_1, R5.pin_1
  N3: R1.Pin_2, R6.Pin_0
  N4: R2.Pin_2, R7.Pin_0
  N5: R3.Pin_2, R8.Pin_0
  N6: R4.Pin_2, R9.Pin_0
  N7: R5.Pin_2, R10.Pin_0
